# Fritzing sketch circuito IoHealth (saved by Fritzing 0.9.3b)
breadboards: 1

parts:
  Componente1 = Arduino Uno (Rev3) - ICSP
  ANT1 = Antenna  # not connected
  Componente2 = Arduino Uno (Rev3)
  VCC2 = 4 x AAA Battery Mount
  R1 = Resistor [tolerance=±5% resistance=220 package="0603 [SMD]"]
  R2 = Resistor [tolerance=±5% resistance=220 package="0603 [SMD]"]
  U2 = Explore PIC Breakout Board [part_number=1N4001 package="300 mil [THT]"]
  Componente3 = Arduino Wireless SD Shield

nets:
  N1: Componente1.A0, R1.Pin_1, R2.Pin_0
  5V: Componente1.5V, Componente3.+5V
  N2: Componente1.D11_PWM/MOSI, U2.pin_19
  N3: Componente1.D0/RX, Componente3.ARDUINO-RX(0)
  N4: Componente1.D1/TX, Componente3.ARDUINO-TX(1)
  N5: Componente1.3V3, U2.pin_39
  N6: Componente1.GND, VCC2.-, R1.Pin_0, U2.pin_38
  N7: Componente1.VIN, VCC2.+, R2.Pin_1
  N8: Componente2.D11_PWM/MOSI, U2.pin_30

notes:
  THINXTRA
  PIC16F18875
  WISOL
  DISPOSITIVOS MEDICOS
  BATERIA 6V
